// Logisim project U2 Digital Logic Project.circ as structural Verilog: 1 circuit, main circuit main
module main (
);

  wire and_1_out, nor_1_out, or_1_out, undriven, undriven_2, undriven_3, undriven_4;

  and and_1 (and_1_out, undriven, undriven_2);
  or or_1 (or_1_out, undriven_3, undriven_4);
  nor nor_1 (nor_1_out, and_1_out, or_1_out);

  // Notes on the sheet:
  //   A
  //   B
  //   C
  //   D
  //   E
  //   F
  //   G
endmodule
