// Logisim project Digital Logic Project U4.circ as structural Verilog: 1 circuit, main circuit main
module main (
  input  A,
  input  B,
  input  C,
  output D,
  output E,
  output F
);

  wire and_1_out, and_2_out, and_3_out, and_4_out, and_5_out, and_6_out;

  LED led_1 (.in(A));
  LED led_2 (.in(A));
  LED led_3 (.in(B));
  buf and_1 (and_1_out, C);  // AND_Gate
  LED led_4 (.in(A));
  LED led_5 (.in(C));
  and and_2 (and_2_out, B, C);
  buf and_3 (and_3_out, B);  // AND_Gate
  LED led_6 (.in(B));
  buf and_4 (and_4_out, A);  // AND_Gate
  LED led_7 (.in(C));
  LED led_8 (.in(B));
  and and_5 (and_5_out, A, C);
  LED led_9 (.in(C));
  and and_6 (and_6_out, A, B);
  and and_7 (F, A, B, C);
  LED led_10 (.in(D));
  or or_1 (D, and_1_out, and_3_out, and_2_out, and_4_out, and_5_out, and_6_out, F);
  LED led_11 (.in(E));
  or or_2 (E, and_2_out, and_5_out, and_6_out);
  LED led_12 (.in(F));
endmodule
